# Fritzing sketch Circuit_Fritzing (saved by Fritzing 0.9.3b)
breadboards: 1

parts:
  Pololu_A1 = Pololu A4988 [package=SO16]
  U1 = NodeMCU V1.0
  M1 = Stepper Motor - Bipolar
  V1 = DC Power [voltage=10]
  C2 = Electrolytic Capacitor [capacitance=100µF package="200 mil [THT, electrolytic]"]
  C3 = Electrolytic Capacitor [capacitance=100µF package="200 mil [THT, electrolytic]"]
  V2 = DC Power [voltage=3.3V]

nets:
  N1: Pololu_A1.MS1, U1.D1
  N2: Pololu_A1.MS2, U1.D2
  N3: Pololu_A1.MS3, U1.D3
  N4: Pololu_A1.RESET, Pololu_A1.SLEEP
  N5: Pololu_A1.STEP, U1.D5
  N6: Pololu_A1.DIR, U1.D6
  GND: Pololu_A1.GND, U1.GND, V1.V-, C2.-, C3.-, V2.V-
  VDD: Pololu_A1.VDD, U1.3V3, C3.+, V2.V+
  N7: Pololu_A1.1B, M1.D
  N8: Pololu_A1.1A, M1.B
  N9: Pololu_A1.2A, M1.C
  N10: Pololu_A1.2B, M1.A
  N11: Pololu_A1.VMOT, V1.V+, C2.+

custom parts:
  NodeMCU V1.0: ESP8266 based NodeMCU
